// Logisim project Mux2Diagram.circ as structural Verilog: 1 circuit, main circuit main
module main (
  input  Y,
  input  in_2,
  input  in_3,
  output out_4
);

  Multiplexer multiplexer_1 (.in0(Y), .in1(in_2), .out(out_4), .sel(in_3));  // open: en
endmodule
