// Logisim project Mux4Diagram.circ as structural Verilog: 1 circuit, main circuit main
module main (
  input  in_1,
  input  in_2,
  input  in_3,
  input  Y,
  input  in_5,
  input  in_6,
  input  in_7,
  input  in_8,
  input  [2:0] in_9,
  output out_10
);

  Multiplexer #(.select(3)) multiplexer_1 (
    .in0(in_1), .in1(in_2), .in2(in_3), .in3(Y), .in4(in_5), .in5(in_6), .in6(in_7), .in7(in_8),
    .out(out_10), .sel(in_9));  // open: en
endmodule
