// Logisim project Buffer.circ as structural Verilog: 1 circuit, main circuit main
module main (
);

  wire buffer_1_out, undriven;

  buf buffer_1 (buffer_1_out, undriven);

  // Notes on the sheet:
  //   IN
  //   OUT
endmodule
